// Logisim project imm-gen.circ as structural Verilog: 1 circuit, main circuit imm_gen
module imm_gen (
  input  [31:0] inst,
  input  [2:0] ImmSel,
  output [31:0] imm
);

  wire B7, B31;
  wire [2:0] B12_14;
  wire [3:0] B8_11;
  wire [4:0] B15_19, B20_24;
  wire [5:0] B25_30;
  wire [31:0] B, bit_extender_4_out, I, J, S, U;

  assign I = {{20{B31}}, {B31, B25_30, B20_24}};  // Bit_Extender bit_extender_1
  assign S = {{20{B31}}, {B31, B25_30, B8_11, B7}};  // Bit_Extender bit_extender_2
  assign B = {{20{B31}}, {B31, B25_30, B8_11, 1'b0}};  // Bit_Extender bit_extender_3
  assign bit_extender_4_out = {{12{B31}}, {B31, B25_30, B20_24, B15_19, B12_14}};  // Bit_Extender bit_extender_4
  assign J = {{11{B31}}, {B31, B15_19, B12_14, B20_24[0], B25_30, B20_24[4:1], 1'b0}};  // Bit_Extender bit_extender_5
  Multiplexer #(.enable("false"), .select(3), .width(32)) multiplexer_1 (
    .in0(I), .in1(S), .in2(B), .in3(U), .in4(J), .out(imm), .sel(ImmSel));  // open: in5, in6, in7
  Shifter #(.width(32)) shifter_1 (.in(bit_extender_4_out), .\dist (5'b01100), .out(U));

  // Notes on the sheet:
  //   INPUTS to your circuit
  //   DON'T CHANGE THE LOCATIONS OF THE INPUTS AND OUTPUTS!
  //   OUTPUT from your circuit
endmodule
